// Logisim project lab2.circ as structural Verilog: 1 circuit, main circuit main
module main (
  input  [7:0] in_1,
  input  in_2,
  input  in_3,
  output [7:0] out_4,
  output out_5
);

  wire O;

  // Probe on in_1
  // Probe on in_1
  and and_1 (O, in_2, in_3);

  assign out_4 = in_1;
  assign out_5 = in_2;

  // Other names for the same wires on the sheet: A = in_2; B = in_3
endmodule
