// Logisim project assignment3.circ as structural Verilog: 1 circuit, main circuit main
module main (
  input  in_1,
  input  in_2,
  input  in_3,
  input  in_4,
  input  in_5,
  input  in_6,
  input  in_7,
  input  C_prime,
  input  in_9,
  input  A,
  input  B,
  input  C,
  output F,
  output G,
  output Sum,
  output Count
);

  wire and_1_out, and_2_out, and_3_out, and_4_out, and_5_out, and_6_out, and_7_out, not_1_out, not_4_out,
       not_5_out, not_6_out, not_7_out, not_8_out, not_9_out, not_10_out, not_11_out, or_1_out, or_2_out,
       or_3_out, undriven;

  not not_1 (not_1_out, in_1);
  // NOT_Gate not_2 has open pins: in=undriven, out=open
  // NOT_Gate not_3 has open pins: in=undriven, out=open
  not not_4 (not_4_out, in_3);
  not not_5 (not_5_out, in_6);
  not not_6 (not_6_out, in_9);
  not not_7 (not_7_out, C_prime);
  not not_8 (not_8_out, C_prime);
  not not_9 (not_9_out, in_7);
  not not_10 (not_10_out, in_7);
  and and_1 (and_1_out, A, C);
  and and_2 (and_2_out, A, B);
  and and_3 (and_3_out, B, C);
  or or_1 (or_1_out, in_2, not_4_out);
  or or_2 (or_2_out, in_4, in_6);
  not not_11 (not_11_out, or_2_out);
  or or_3 (or_3_out, not_5_out, in_5);
  and and_4 (and_4_out, not_6_out, not_7_out, in_7);
  and and_5 (and_5_out, in_9, not_8_out, not_9_out);
  and and_6 (and_6_out, in_9, C_prime, in_7);
  and and_7 (and_7_out, in_9, C_prime, not_10_out);
  and and_8 (F, not_1_out, or_1_out);
  and and_9 (G, not_11_out, or_3_out);
  or or_4 (Sum, and_4_out, and_5_out, and_6_out, and_7_out);
  or or_5 (Count, and_1_out, and_2_out, and_3_out);

  // Notes on the sheet:
  //   G = (A+C)'(B+C')
  //   AB'C'+A'B'C+ABC+A'BC
  //   B'
  //   B'
  //   A'
  //   A'
  //   AC+AB+BC
  //   A'
  //   C'
  //   A+C
  //   C'
  //   B+C'
  //   AC
  //   AB
  //   BC
  //   F = A'(B+C')     
  //   B+C'
  //   (A+C')
  //   AB'C'
  //   A'B'C
  //   ABC
  //   A'BC
  //   A'(B+C')
  //    (A+C)'(B+C')
  //   AB'C'+A'B'C+ABC+A'BC
  //   AC+AB+BC
endmodule
