// Logisim project lab3.circ as structural Verilog: 1 circuit, main circuit main
module main (
  input  A,
  input  B,
  input  C,
  output out_4,
  output out_5,
  output A___BC,
  output A_B__A_C
);

  wire and_1_out, not_1_out, not_2_out, or_2_out, or_3_out;

  nand nand_1 (out_4, A, B);
  not not_1 (not_1_out, A);
  or or_1 (out_5, not_1_out, not_2_out);
  not not_2 (not_2_out, B);
  and and_1 (and_1_out, B, C);
  or or_2 (or_2_out, A, B);
  or or_3 (or_3_out, A, C);
  LED led_1 (.in(out_4));
  LED led_2 (.in(out_5));
  or or_4 (A___BC, and_1_out, A);
  and and_2 (A_B__A_C, or_2_out, or_3_out);

  // Notes on the sheet:
  //   BC
  //   A + B
  //   A+C
endmodule
