// Logisim project logisim_lab_3.circ as structural Verilog: 3 circuits, main circuit main
module main (
  input  A,
  input  B,
  input  C,
  output out_4,
  output out_5
);

  circuit_1 I (.C(C), .A(A), .B(B), .X(out_4));
  circuit_2 II (.C(C), .A(A), .B(B), .X(out_5));
endmodule

module circuit_1 (
  input  A,
  input  B,
  input  C,
  output X
);

  wire and_1_out, and_2_out, and_3_out, and_4_out, and_5_out, and_6_out, not_1_out, not_2_out, not_3_out,
       not_4_out;

  and and_1 (and_1_out, A, C);
  not not_1 (not_1_out, B);
  and and_2 (and_2_out, C, not_2_out);
  not not_2 (not_2_out, B);
  not not_3 (not_3_out, A);
  and and_3 (and_3_out, B, A);
  not not_4 (not_4_out, C);
  and and_4 (and_4_out, and_1_out, not_1_out);
  and and_5 (and_5_out, and_2_out, not_3_out);
  and and_6 (and_6_out, and_3_out, not_4_out);
  or or_1 (X, and_4_out, and_5_out, and_6_out);

  // Notes on the sheet:
  //   I
endmodule

module circuit_2 (
  input  A,
  input  B,
  input  C,
  output X
);

  wire nand_1_out, nand_2_out, nand_3_out, nand_4_out, nand_5_out, nand_6_out;

  nand nand_1 (nand_1_out, 1'b1, A);
  nand nand_2 (nand_2_out, 1'b1, B);
  nand nand_3 (nand_3_out, 1'b1, C);
  nand nand_4 (nand_4_out, A, C, nand_2_out);
  nand nand_5 (nand_5_out, C, nand_2_out, nand_1_out);
  nand nand_6 (nand_6_out, B, A, nand_3_out);
  nand nand_7 (X, nand_4_out, nand_5_out, nand_6_out);

  // Notes on the sheet:
  //   II
endmodule
