// Logisim project lab_4idk.circ as structural Verilog: 3 circuits, main circuit main
module main (
  input  in_1,
  input  in_2,
  input  in_3,
  input  in_4,
  input  in_5,
  input  in_6,
  input  in_7,
  input  in_8,
  input  in_9,
  output out_10,
  output out_11,
  output out_12,
  output out_13,
  output out_14
);

  wire fulladder1bit_1_cout, fulladder1bit_2_cout, fulladder1bit_3_cout;

  FullAdder1Bit fulladder1bit_1 (.Cin(in_1), .A(in_2), .B(in_6), .Cout(fulladder1bit_1_cout), .Sum(out_10));
  FullAdder1Bit fulladder1bit_2 (
    .Cin(fulladder1bit_1_cout), .A(in_3), .B(in_7), .Cout(fulladder1bit_2_cout), .Sum(out_11));
  FullAdder1Bit fulladder1bit_3 (
    .Cin(fulladder1bit_2_cout), .A(in_4), .B(in_8), .Cout(fulladder1bit_3_cout), .Sum(out_12));
  FullAdder1Bit fulladder1bit_4 (.Cin(fulladder1bit_3_cout), .A(in_5), .B(in_9), .Cout(out_14), .Sum(out_13));

  // Other names for the same wires on the sheet: A0 = in_2; A1 = in_3; A2 = in_4; A3 = in_5; B0 = in_6; B1 = in_7;
  //   B2 = in_8; B3 = in_9
endmodule

module lab4 (
  input  A,
  input  B,
  input  Cin,
  output Sum,
  output Cout
);

  wire and_1_out, and_2_out, and_3_out, and_4_out, and_5_out, and_6_out, and_7_out, not_1_out, not_2_out,
       not_3_out;

  not not_1 (not_1_out, A);
  not not_2 (not_2_out, B);
  not not_3 (not_3_out, Cin);
  and and_1 (and_1_out, not_1_out, not_2_out, Cin);
  and and_2 (and_2_out, not_1_out, B, not_3_out);
  and and_3 (and_3_out, A, not_2_out, not_3_out);
  and and_4 (and_4_out, A, B, Cin);
  and and_5 (and_5_out, B, Cin);
  and and_6 (and_6_out, A, Cin);
  and and_7 (and_7_out, A, B);
  or or_1 (Sum, and_1_out, and_2_out, and_3_out, and_4_out);
  or or_2 (Cout, and_5_out, and_6_out, and_7_out);
endmodule

module FullAdder1Bit (
  input  A,
  input  B,
  input  Cin,
  output Cout,
  output Sum
);

  wire and_1_out, and_2_out, and_3_out, and_4_out, and_5_out, and_6_out, and_7_out, not_1_out, not_2_out,
       not_3_out;

  not not_1 (not_1_out, A);
  not not_2 (not_2_out, B);
  not not_3 (not_3_out, Cin);
  and and_1 (and_1_out, B, Cin);
  and and_2 (and_2_out, A, Cin);
  and and_3 (and_3_out, A, B);
  and and_4 (and_4_out, not_1_out, not_2_out, Cin);
  and and_5 (and_5_out, not_1_out, B, not_3_out);
  and and_6 (and_6_out, A, not_2_out, not_3_out);
  and and_7 (and_7_out, A, B, Cin);
  or or_1 (Cout, and_1_out, and_2_out, and_3_out);
  or or_2 (Sum, and_4_out, and_5_out, and_6_out, and_7_out);
endmodule
