// Logisim project lab_5.circ as structural Verilog: 3 circuits, main circuit main
module main (
  input  INVB,
  input  INVA,
  input  in_3,
  input  in_4,
  input  in_5,
  input  in_6,
  input  in_7,
  input  in_8,
  input  in_9,
  input  in_10,
  input  in_11,
  output out_12,
  output out_13,
  output out_14,
  output out_15,
  output out_16
);

  wire fulladder1bit_1_cout, fulladder1bit_2_cout, fulladder1bit_3_cout, xor_1_out, xor_2_out, xor_3_out,
       xor_4_out, xor_5_out, xor_6_out, xor_7_out, xor_8_out;

  xor xor_1 (xor_1_out, INVA, in_4);
  xor xor_2 (xor_2_out, in_8, INVB);
  xor xor_3 (xor_3_out, INVA, in_5);
  xor xor_4 (xor_4_out, in_9, INVB);
  xor xor_5 (xor_5_out, INVA, in_6);
  xor xor_6 (xor_6_out, in_10, INVB);
  xor xor_7 (xor_7_out, INVA, in_7);
  xor xor_8 (xor_8_out, in_11, INVB);
  FullAdder1Bit fulladder1bit_1 (.Cin(in_3), .A(xor_1_out), .B(xor_2_out), .Cout(fulladder1bit_1_cout), .Sum(out_12));
  FullAdder1Bit fulladder1bit_2 (
    .Cin(fulladder1bit_1_cout), .A(xor_3_out), .B(xor_4_out), .Cout(fulladder1bit_2_cout), .Sum(out_13));
  FullAdder1Bit fulladder1bit_3 (
    .Cin(fulladder1bit_2_cout), .A(xor_5_out), .B(xor_6_out), .Cout(fulladder1bit_3_cout), .Sum(out_14));
  FullAdder1Bit fulladder1bit_4 (.Cin(fulladder1bit_3_cout), .A(xor_7_out), .B(xor_8_out), .Cout(out_16), .Sum(out_15));

  // Other names for the same wires on the sheet: A0 = in_4; A1 = in_5; A2 = in_6; A3 = in_7; B0 = in_8; B1 = in_9;
  //   B2 = in_10; B3 = in_11
endmodule

module lab4 (
  input  A,
  input  B,
  input  Cin,
  output Sum,
  output Cout
);

  wire and_1_out, and_2_out, and_3_out, and_4_out, and_5_out, and_6_out, and_7_out, not_1_out, not_2_out,
       not_3_out;

  not not_1 (not_1_out, A);
  not not_2 (not_2_out, B);
  not not_3 (not_3_out, Cin);
  and and_1 (and_1_out, not_1_out, not_2_out, Cin);
  and and_2 (and_2_out, not_1_out, B, not_3_out);
  and and_3 (and_3_out, A, not_2_out, not_3_out);
  and and_4 (and_4_out, A, B, Cin);
  and and_5 (and_5_out, B, Cin);
  and and_6 (and_6_out, A, Cin);
  and and_7 (and_7_out, A, B);
  or or_1 (Sum, and_1_out, and_2_out, and_3_out, and_4_out);
  or or_2 (Cout, and_5_out, and_6_out, and_7_out);
endmodule

module FullAdder1Bit (
  input  A,
  input  B,
  input  Cin,
  output Cout,
  output Sum
);

  wire and_1_out, and_2_out, and_3_out, and_4_out, and_5_out, and_6_out, and_7_out, not_1_out, not_2_out,
       not_3_out;

  not not_1 (not_1_out, A);
  not not_2 (not_2_out, B);
  not not_3 (not_3_out, Cin);
  and and_1 (and_1_out, B, Cin);
  and and_2 (and_2_out, A, Cin);
  and and_3 (and_3_out, A, B);
  and and_4 (and_4_out, not_1_out, not_2_out, Cin);
  and and_5 (and_5_out, not_1_out, B, not_3_out);
  and and_6 (and_6_out, A, not_2_out, not_3_out);
  and and_7 (and_7_out, A, B, Cin);
  or or_1 (Cout, and_1_out, and_2_out, and_3_out);
  or or_2 (Sum, and_4_out, and_5_out, and_6_out, and_7_out);
endmodule
