// Logisim project cpu.circ as structural Verilog: 2 circuits, main circuit main
module main (
  input  F0,
  input  F1,
  input  ENA,
  input  ENB,
  input  INVA,
  input  in_6,
  input  A,
  input  in_8,
  input  in_9,
  input  in_10,
  input  in_11,
  input  in_12,
  input  in_13,
  input  in_14,
  input  B,
  input  in_16,
  input  in_17,
  input  in_18,
  input  in_19,
  input  in_20,
  input  in_21,
  input  in_22,
  output [7:0] O,
  output [7:0] out_24,
  output out_25
);

  wire alu_1bit_1_cout, alu_1bit_2_cout, alu_1bit_3_cout, alu_1bit_4_cout, alu_1bit_5_cout, alu_1bit_6_cout,
       alu_1bit_7_cout;

  ALU_1bit alu_1bit_1 (
    .F0(F0), .F1(F1), .INVA(INVA), .A(in_14), .ENA(ENA), .B(in_22), .ENB(ENB), .Cin(in_6),
    .Cout(alu_1bit_1_cout), .O(O[0]));
  ALU_1bit alu_1bit_2 (
    .F0(F0), .F1(F1), .INVA(INVA), .A(in_13), .ENA(ENA), .B(in_21), .ENB(ENB), .Cin(alu_1bit_1_cout),
    .Cout(alu_1bit_2_cout), .O(O[1]));
  ALU_1bit alu_1bit_3 (
    .F0(F0), .F1(F1), .INVA(INVA), .A(in_12), .ENA(ENA), .B(in_20), .ENB(ENB), .Cin(alu_1bit_2_cout),
    .Cout(alu_1bit_3_cout), .O(O[2]));
  ALU_1bit alu_1bit_4 (
    .F0(F0), .F1(F1), .INVA(INVA), .A(in_11), .ENA(ENA), .B(in_19), .ENB(ENB), .Cin(alu_1bit_3_cout),
    .Cout(alu_1bit_4_cout), .O(O[3]));
  ALU_1bit alu_1bit_5 (
    .F0(F0), .F1(F1), .INVA(INVA), .A(in_10), .ENA(ENA), .B(in_18), .ENB(ENB), .Cin(alu_1bit_4_cout),
    .Cout(alu_1bit_5_cout), .O(O[4]));
  ALU_1bit alu_1bit_6 (
    .F0(F0), .F1(F1), .INVA(INVA), .A(in_9), .ENA(ENA), .B(in_17), .ENB(ENB), .Cin(alu_1bit_5_cout),
    .Cout(alu_1bit_6_cout), .O(O[5]));
  ALU_1bit alu_1bit_7 (
    .F0(F0), .F1(F1), .INVA(INVA), .A(in_8), .ENA(ENA), .B(in_16), .ENB(ENB), .Cin(alu_1bit_6_cout),
    .Cout(alu_1bit_7_cout), .O(O[6]));
  ALU_1bit alu_1bit_8 (
    .F0(F0), .F1(F1), .INVA(INVA), .A(A), .ENA(ENA), .B(B), .ENB(ENB), .Cin(alu_1bit_7_cout), .Cout(out_25),
    .O(O[7]));

  assign out_24 = O;

  // Other names for the same wires on the sheet: A0 = in_14; A1 = in_13; A2 = in_12; A3 = in_11; A4 = in_10;
  //   A5 = in_9; A6 = in_8; A7 = A; B0 = in_22; B1 = in_21; B2 = in_20; B3 = in_19; B4 = in_18; B5 = in_17;
  //   B6 = in_16; B7 = B; CO = out_25
endmodule

module ALU_1bit (
  input  Cin,
  input  INVA,
  input  A,
  input  ENA,
  input  B,
  input  ENB,
  input  F0,
  input  F1,
  output O,
  output Cout
);

  wire and_1_out, and_2_out, and_3_out, and_4_out, and_5_out, and_6_out, and_7_out, and_8_out, and_9_out,
       and_10_out, and_11_out, and_12_out, and_13_out, not_1_out, not_2_out, not_3_out, not_4_out, not_5_out,
       or_1_out, xor_1_out, xor_2_out, xor_3_out;

  and and_1 (and_1_out, A, ENA);
  and and_2 (and_2_out, B, ENB);
  not not_1 (not_1_out, F0);
  not not_2 (not_2_out, F1);
  not not_3 (not_3_out, F0);
  not not_4 (not_4_out, F1);
  xor xor_1 (xor_1_out, INVA, and_1_out);
  and and_3 (and_3_out, not_1_out, not_2_out);
  and and_4 (and_4_out, not_3_out, F1);
  and and_5 (and_5_out, F0, not_4_out);
  and and_6 (and_6_out, F0, F1);
  not not_5 (not_5_out, and_2_out);
  and and_7 (and_7_out, xor_1_out, and_2_out);
  or or_1 (or_1_out, xor_1_out, and_2_out);
  and and_8 (and_8_out, and_7_out, and_3_out);
  and and_9 (and_9_out, or_1_out, and_4_out);
  and and_10 (and_10_out, not_5_out, and_5_out);
  and and_11 (and_11_out, and_6_out, xor_1_out, and_2_out);
  xor xor_2 (xor_2_out, and_2_out, xor_1_out);
  and and_12 (and_12_out, and_6_out, xor_2_out, Cin);
  or or_2 (Cout, and_11_out, and_12_out);
  xor xor_3 (xor_3_out, Cin, xor_2_out);
  and and_13 (and_13_out, xor_3_out, and_6_out);
  or or_3 (O, and_8_out, and_9_out, and_10_out, and_13_out);
endmodule
