// Logisim project lab6.circ as structural Verilog: 2 circuits, main circuit main
module main (
  input  F1,
  input  F0,
  input  ENB,
  input  ENA,
  input  INVA,
  input  in_6,
  input  A,
  input  in_8,
  input  in_9,
  input  in_10,
  input  B,
  input  in_12,
  input  in_13,
  input  in_14,
  output out_15,
  output out_16,
  output out_17,
  output out_18,
  output out_19
);

  wire alu_1bit_1_cout, alu_1bit_2_cout, alu_1bit_3_cout;

  ALU_1bit alu_1bit_1 (
    .F0(F0), .F1(F1), .INVA(INVA), .A(in_10), .ENA(ENA), .B(in_14), .ENB(ENB), .Cin(in_6),
    .Cout(alu_1bit_1_cout), .O(out_19));
  ALU_1bit alu_1bit_2 (
    .F0(F0), .F1(F1), .INVA(INVA), .A(in_9), .ENA(ENA), .B(in_13), .ENB(ENB), .Cin(alu_1bit_1_cout),
    .Cout(alu_1bit_2_cout), .O(out_18));
  ALU_1bit alu_1bit_3 (
    .F0(F0), .F1(F1), .INVA(INVA), .A(in_8), .ENA(ENA), .B(in_12), .ENB(ENB), .Cin(alu_1bit_2_cout),
    .Cout(alu_1bit_3_cout), .O(out_17));
  ALU_1bit alu_1bit_4 (
    .F0(F0), .F1(F1), .INVA(INVA), .A(A), .ENA(ENA), .B(B), .ENB(ENB), .Cin(alu_1bit_3_cout), .Cout(out_15),
    .O(out_16));

  // Other names for the same wires on the sheet: A0 = in_10; A1 = in_9; A2 = in_8; A3 = A; B0 = in_14; B1 = in_13;
  //   B2 = in_12; B3 = B; CO = out_15; O0 = out_19; O1 = out_18; O2 = out_17; O3 = out_16
endmodule

module ALU_1bit (
  input  Cin,
  input  INVA,
  input  A,
  input  ENA,
  input  B,
  input  ENB,
  input  F0,
  input  F1,
  output O,
  output Cout
);

  wire and_1_out, and_2_out, and_3_out, and_4_out, and_5_out, and_6_out, and_7_out, and_8_out, and_9_out,
       and_10_out, and_11_out, and_12_out, and_13_out, not_1_out, not_2_out, not_3_out, not_4_out, not_5_out,
       or_1_out, xor_1_out, xor_2_out, xor_3_out;

  and and_1 (and_1_out, A, ENA);
  and and_2 (and_2_out, B, ENB);
  not not_1 (not_1_out, F0);
  not not_2 (not_2_out, F1);
  not not_3 (not_3_out, F0);
  not not_4 (not_4_out, F1);
  xor xor_1 (xor_1_out, INVA, and_1_out);
  and and_3 (and_3_out, not_1_out, not_2_out);
  and and_4 (and_4_out, not_3_out, F1);
  and and_5 (and_5_out, F0, not_4_out);
  and and_6 (and_6_out, F0, F1);
  not not_5 (not_5_out, and_2_out);
  and and_7 (and_7_out, xor_1_out, and_2_out);
  or or_1 (or_1_out, xor_1_out, and_2_out);
  and and_8 (and_8_out, and_7_out, and_3_out);
  and and_9 (and_9_out, or_1_out, and_4_out);
  and and_10 (and_10_out, not_5_out, and_5_out);
  and and_11 (and_11_out, and_6_out, xor_1_out, and_2_out);
  xor xor_2 (xor_2_out, and_2_out, xor_1_out);
  and and_12 (and_12_out, and_6_out, xor_2_out, Cin);
  or or_2 (Cout, and_11_out, and_12_out);
  xor xor_3 (xor_3_out, Cin, xor_2_out);
  and and_13 (and_13_out, xor_3_out, and_6_out);
  or or_3 (O, and_8_out, and_9_out, and_10_out, and_13_out);
endmodule
