// Logisim project mem12.circ as structural Verilog
module D (
  input  in_1,
  input  CK,
  output out_3
);

  D_Flip_Flop d_ff_1 (.clk(CK), .D(in_1), .Q(out_3));  // open: Qn, preset, reset
endmodule

module mem12 (
);

  D d_1 ();  // open: CK, in_1, out_3
  Controlled_Buffer controlled_buffer_1 ();  // open: in, out, en
endmodule
