// Logisim project ev_mem12.circ as structural Verilog: 3 circuits, main circuit main
module main (
  input  [2:0] in_1,
  input  [1:0] in_2,
  input  in_3,
  input  in_4,
  input  in_5
);

  wire [2:0] mem12_1_o0;

  mem12 mem12_1 (
    .I2(in_1[2]), .I1(in_1[1]), .I0(in_1[0]), .A1(in_2[1]), .A0(in_2[0]), .CS(in_3), .RD(in_4), .OE(in_5),
    .O2(mem12_1_o0[2]), .O1(mem12_1_o0[1]), .O0(mem12_1_o0[0]));
  Hex_Digit_Display hex_digit_display_1 (.value({1'b0, mem12_1_o0}));  // open: dp
endmodule

module D (
  input  in_1,
  input  CK,
  output out_3
);

  D_Flip_Flop d_ff_1 (.clk(CK), .D(in_1), .Q(out_3));  // open: Qn, preset, reset
endmodule

module mem12 (
  input  I2,
  input  I1,
  input  I0,
  input  A1,
  input  A0,
  input  CS,
  input  RD,
  input  OE,
  output O2,
  output O1,
  output O0
);

  wire and_1_out, and_2_out, and_3_out, and_4_out, and_5_out, and_6_out, and_7_out, and_8_out, and_9_out,
       and_10_out, and_11_out, and_12_out, and_13_out, and_14_out, and_15_out, and_16_out, and_17_out,
       and_18_out, and_19_out, and_20_out, and_21_out, and_22_out, d_1_out_3, d_2_out_3, d_3_out_3,
       d_4_out_3, d_5_out_3, d_6_out_3, d_7_out_3, d_8_out_3, d_9_out_3, d_10_out_3, d_11_out_3, d_12_out_3,
       not_1_out, not_2_out, not_3_out, not_4_out, not_5_out, or_1_out, or_2_out, or_3_out;

  not not_1 (not_1_out, A1);
  not not_2 (not_2_out, A0);
  not not_3 (not_3_out, A1);
  not not_4 (not_4_out, A0);
  and and_1 (and_1_out, not_1_out, not_2_out);
  and and_2 (and_2_out, not_3_out, A0);
  and and_3 (and_3_out, A1, not_4_out);
  and and_4 (and_4_out, A1, A0);
  and and_5 (and_5_out, not_5_out, CS);
  not not_5 (not_5_out, RD);
  and and_6 (and_6_out, and_5_out, and_1_out);
  and and_7 (and_7_out, and_5_out, and_2_out);
  and and_8 (and_8_out, and_5_out, and_3_out);
  and and_9 (and_9_out, and_5_out, and_4_out);
  and and_10 (and_10_out, CS, RD, OE);
  D d_1 (.CK(and_6_out), .in_1(I0), .out_3(d_1_out_3));
  D d_2 (.CK(and_7_out), .in_1(I0), .out_3(d_2_out_3));
  D d_3 (.CK(and_8_out), .in_1(I0), .out_3(d_3_out_3));
  and and_11 (and_11_out, d_3_out_3, and_3_out);
  D d_4 (.CK(and_9_out), .in_1(I0), .out_3(d_4_out_3));
  and and_12 (and_12_out, d_4_out_3, and_4_out);
  and and_13 (and_13_out, d_1_out_3, and_1_out);
  and and_14 (and_14_out, d_2_out_3, and_2_out);
  or or_1 (or_1_out, and_12_out, and_11_out, and_14_out, and_13_out);
  D d_5 (.CK(and_6_out), .in_1(I1), .out_3(d_5_out_3));
  D d_6 (.CK(and_7_out), .in_1(I1), .out_3(d_6_out_3));
  D d_7 (.CK(and_8_out), .in_1(I1), .out_3(d_7_out_3));
  and and_15 (and_15_out, d_7_out_3, and_3_out);
  D d_8 (.CK(and_9_out), .in_1(I1), .out_3(d_8_out_3));
  and and_16 (and_16_out, d_8_out_3, and_4_out);
  and and_17 (and_17_out, d_5_out_3, and_1_out);
  and and_18 (and_18_out, d_6_out_3, and_2_out);
  or or_2 (or_2_out, and_16_out, and_15_out, and_18_out, and_17_out);
  D d_9 (.CK(and_6_out), .in_1(I2), .out_3(d_9_out_3));
  D d_10 (.CK(and_7_out), .in_1(I2), .out_3(d_10_out_3));
  and and_19 (and_19_out, d_10_out_3, and_2_out);
  D d_11 (.CK(and_8_out), .in_1(I2), .out_3(d_11_out_3));
  and and_20 (and_20_out, d_11_out_3, and_3_out);
  D d_12 (.CK(and_9_out), .in_1(I2), .out_3(d_12_out_3));
  and and_21 (and_21_out, d_12_out_3, and_4_out);
  or or_3 (or_3_out, and_21_out, and_20_out, and_19_out, and_22_out);
  and and_22 (and_22_out, d_9_out_3, and_1_out);
  assign O2 = and_10_out ? or_3_out : 1'bz;  // Controlled_Buffer controlled_buffer_1
  assign O1 = and_10_out ? or_2_out : 1'bz;  // Controlled_Buffer controlled_buffer_2
  assign O0 = and_10_out ? or_1_out : 1'bz;  // Controlled_Buffer controlled_buffer_3

  // Notes on the sheet:
  //   Data In
  //   Word 0
  //   select Line
  //   Word 1
  //   select Line
  //   Word 2
  //   select Line
  //   CS * RD'
  //   Write gate
  //   Output enable = CS * RD * OE
  //   Word 0
  //   Word 1
  //   Word 2
  //   Word 3
endmodule
