// Logisim project ev_parity.circ as structural Verilog: 4 circuits, main circuit main
module main (
  input  [3:0] in_1,
  output a,
  output b,
  output c,
  output d,
  output x,
  output y,
  output z
);

  xor xor_1 (x, in_1[3], in_1[2], in_1[0]);
  xor xor_2 (y, in_1[3], in_1[1], in_1[0]);
  xor xor_3 (z, in_1[2], in_1[1], in_1[0]);

  assign a = in_1[3];
  assign b = in_1[2];
  assign c = in_1[1];
  assign d = in_1[0];
endmodule

module xyz (
  input  [3:0] in_1
);

  wire x, y, z;

  LED a (.in(in_1[3]));
  LED u_x (.in(x));
  LED u_y (.in(y));
  xor xor_1 (x, in_1[3], in_1[2], in_1[0]);
  xor xor_2 (y, in_1[3], in_1[1], in_1[0]);
  LED b (.in(in_1[2]));
  LED c (.in(in_1[1]));
  LED d (.in(in_1[0]));
  LED u_z (.in(z));
  xor xor_3 (z, in_1[2], in_1[1], in_1[0]);

  // Other names for the same wires on the sheet: d = in_1[0]; c = in_1[1]; b = in_1[2]; a = in_1[3]
endmodule

module error_detection (
  input  [6:0] in_1
);

  wire xor_1_out, xor_2_out, xor_3_out, xor_4_out, xor_5_out, xor_6_out;
  wire [2:0] display_1_i0;

  LED x (.in(in_1[6]));
  LED y (.in(in_1[5]));
  LED a (.in(in_1[4]));
  LED z (.in(in_1[3]));
  LED b (.in(in_1[2]));
  LED c (.in(in_1[1]));
  LED d (.in(in_1[0]));
  xor xor_1 (xor_1_out, in_1[4], in_1[2], in_1[0]);
  xor xor_2 (xor_2_out, in_1[4], in_1[1], in_1[0]);
  xor xor_3 (xor_3_out, in_1[2], in_1[1], in_1[0]);
  xor xor_4 (xor_4_out, xor_1_out, in_1[6]);
  xor xor_5 (xor_5_out, xor_2_out, in_1[5]);
  xor xor_6 (xor_6_out, xor_3_out, in_1[3]);
  Hex_Digit_Display hex_digit_display_1 (.value({1'b0, display_1_i0}));  // open: dp
  display display_1 (
    .z(xor_6_out), .x(xor_4_out), .y(xor_5_out), .I0(display_1_i0[0]), .I2(display_1_i0[2]),
    .I1(display_1_i0[1]));

  // Other names for the same wires on the sheet: d = in_1[0]; c = in_1[1]; b = in_1[2]; z = in_1[3]; a = in_1[4];
  //   y = in_1[5]; x = in_1[6]
endmodule

module display (
  input  x,
  input  y,
  input  z,
  output I2,
  output I1,
  output I0
);

  wire and_1_out, and_2_out, not_1_out;

  not not_1 (not_1_out, z);
  and and_1 (and_1_out, y, not_1_out);
  or or_1 (I1, and_1_out, and_2_out);
  and and_2 (and_2_out, x, y);

  assign I0 = x;
  assign I2 = z;
endmodule
