// Logisim project parity.circ as structural Verilog: 1 circuit, main circuit main
module main (
  input  in_1,
  input  a,
  input  b,
  input  c,
  input  d,
  input  in_6,
  input  in_7,
  output out_8,
  output x,
  output y,
  output ao,
  output z,
  output bo,
  output co,
  output \do 
);

  xor xor_1 (x, a, b, d);
  xor xor_2 (y, a, c, d);
  xor xor_3 (z, b, c, d);
  LED led_1 (.in(x));
  LED led_2 (.in(y));
  LED led_3 (.in(a));
  LED led_4 (.in(z));
  LED led_5 (.in(b));
  LED led_6 (.in(c));
  LED led_7 (.in(d));
  xor xor_4 (out_8, in_1, in_6, in_7);

  assign ao = a;
  assign bo = b;
  assign co = c;
  assign \do  = d;
endmodule
