// Logisim project lab1.circ as structural Verilog: 2 circuits, main circuit main
module main (
  input  [3:0] in_1,
  input  [7:0] A,
  input  [7:0] B,
  output [7:0] out_4
);

  XOR2 xor2_1 ();  // open: A, B, out_3
  // Probe on A
  // Probe on B
  assign out_4 = A | B;  // OR_Gate or_1, 8 bits wide
  // Probe on out_4
  LED led_1 (.in(in_1[3]));
  LED led_2 (.in(in_1[2]));
  LED led_3 (.in(in_1[1]));
  LED led_4 (.in(in_1[0]));
endmodule

module XOR2 (
  input  A,
  input  B,
  output out_3
);

  wire and_1_out, and_2_out, not_1_out, not_2_out;

  not not_1 (not_1_out, A);
  and and_1 (and_1_out, not_1_out, B);
  and and_2 (and_2_out, A, not_2_out);
  not not_2 (not_2_out, B);
  or or_1 (out_3, and_1_out, and_2_out);
endmodule
